# Fritzing sketch Diagrama Final (saved by Fritzing 1.0.4)
breadboards: 1

parts:
  Componente1 = Arduino Mega 2560 (Rev3)
  Componente2 = Adafruit TCA9548A
  LCD1 = 20x4 LCD display [part_number=2004A]
  LCM1602_IIC1 = LCM1602 IIC [part_number="LCM1602 IIC" chip_label="LCM1602 IIC" package="DIP (Dual Inline) [THT]"]
  ZS-042_RTC1 = ZS-042 RTC Module
  M1 = BME280
  Componente3 = BH1750
  Mod1 = gy-906
  PART1 = ML8511 UV Sensor Breakout [part_number=SEN-12705]
  M2 = MQ-135 Air Quality Sensor Module
  Mod2 = KY-023 Dual Axis Joystick Module [package="Breakout board"]
  Capacitive_Soil_Moisture_Sensor1 = DFRobot Capacitive Soil Moisture Sensor V1.0 [part_number=SEN0193]
  microSD1 = MicroSD Card Module
  DS18B1 = DS18B20 1-Wire Temperature Sensor Module [part_number=DS18B20]
  R1 = Resistor [tolerance=±5% power=0.25W resistance=220 package=THT]
  S1 = Pushbutton [package="[THT]"]
  S2 = Pushbutton [package="[THT]"]
  LED1 = LED - 5mm [color="Red (633nm)" current=0.030A package="5 mm [THT]"]
  LED2 = LED - 5mm [color="Red (633nm)" current=0.030A package="5 mm [THT]"]
  LED3 = LED - 5mm [color="Red (633nm)" current=0.030A package="5 mm [THT]"]
  LED4 = LED - 5mm [color="Red (633nm)" current=0.030A package="5 mm [THT]"]
  LED5 = LED - 5mm [color="Red (633nm)" current=0.030A package="5 mm [THT]"]
  R3 = Resistor [tolerance=±5% power=0.25W resistance=220 package=THT]
  R4 = Resistor [tolerance=±5% power=0.25W resistance=220 package=THT]
  R5 = Resistor [tolerance=±5% power=0.25W resistance=220 package=THT]
  R6 = Resistor [tolerance=±5% power=0.25W resistance=220 package=THT]
  R7 = Resistor [tolerance=±5% power=0.25W resistance=220 package=THT]
  R8 = Resistor [tolerance=±5% power=0.25W resistance=220 package=THT]
  R9 = Resistor [tolerance=±5% power=0.25W resistance=220 package=THT]
  R10 = Resistor [tolerance=±5% power=0.25W resistance=220 package=THT]

nets:
  N1: Componente1.A10, Mod2.VRy
  N2: Componente1.A11, Mod2.VRx
  N3: Componente1.A12, M2.AO
  N4: Componente1.A13, PART1.OUT
  N5: Componente1.A14, PART1.EN
  N6: Componente1.A15, Capacitive_Soil_Moisture_Sensor1.A
  N7: Componente1.D21/SCL, Componente2.INPUTSCL
  N8: Componente1.D20/SDA, Componente2.INPUTSDA
  GND: Componente1.GND, Componente2.GND, LCM1602_IIC1.GND, ZS-042_RTC1.GND, M1.GND, Componente3.GND, Mod1.GND, PART1.GND, M2.GND, Mod2.GND, Capacitive_Soil_Moisture_Sensor1.GND, microSD1.GND, DS18B1.GND, R1.Pin_0, LED1.cathode, LED2.cathode, LED3.cathode, LED4.cathode, LED5.cathode, R3.Pin_1, R9.Pin_0, R10.Pin_0
  N9: Componente1.D13_PWM, microSD1.SCK
  N10: Componente1.D12_PWM, microSD1.MISO
  N11: Componente1.D11_PWM, microSD1.MOSI
  N12: Componente1.D10_PWM, microSD1.CS
  N13: Componente1.D9_PWM, DS18B1.OUT, R1.Pin_1
  N14: Componente1.D8_PWM, S1.Pin_3, S1.Pin_4
  3V3: Componente1.3V3, M1.VIN, PART1.3.3V
  VCC: Componente1.5V, Componente2.VCC, LCM1602_IIC1.VCC, ZS-042_RTC1.VCC, Componente3.VCC, Mod1.VIN, M2.VCC, Mod2.+5V, Capacitive_Soil_Moisture_Sensor1.VCC, microSD1.VCC, DS18B1.VDD
  N15: Componente1.D2_PWM, R8.Pin_0
  N16: Componente1.D3_PWM, R7.Pin_0
  N17: Componente1.D4_PWM, R6.Pin_0
  N18: Componente1.D5_PWM, R5.Pin_0
  N19: Componente1.D6_PWM, R4.Pin_0
  N20: Componente1.D7_PWM, S2.Pin_3, S2.Pin_4
  N21: Componente2.3SDA, Mod1.SDA
  N22: Componente2.3SCL, Mod1.SCL
  N23: Componente2.4SDA, Componente3.SDA
  N24: Componente2.4SCL, Componente3.SCL
  N25: Componente2.5SDA, M1.SDA
  N26: Componente2.5SCL, M1.SCL
  N27: Componente2.6SDA, ZS-042_RTC1.SDA
  N28: Componente2.6SCL, ZS-042_RTC1.SCL
  N29: Componente2.7SDA, LCM1602_IIC1.SDA
  N30: Componente2.7SCL, LCM1602_IIC1.SCL
  VSS: LCD1.Vss, LCM1602_IIC1.VSS
  VDD: LCD1.Vdd, LCM1602_IIC1.VDD
  N31: LCD1.Vo, LCM1602_IIC1.V0
  N32: LCD1.RS, LCM1602_IIC1.RS
  N33: LCD1.R/W, LCM1602_IIC1.RW
  N34: LCD1.E, LCM1602_IIC1.E
  N35: LCD1.DB0, LCM1602_IIC1.D0
  N36: LCD1.DB1, LCM1602_IIC1.D1
  N37: LCD1.DB2, LCM1602_IIC1.D2
  N38: LCD1.DB3, LCM1602_IIC1.D3
  N39: LCD1.DB4, LCM1602_IIC1.D4
  N40: LCD1.DB5, LCM1602_IIC1.D5
  N41: LCD1.DB6, LCM1602_IIC1.D6
  N42: LCD1.DB7, LCM1602_IIC1.D7
  N43: LCD1.A_+, LCM1602_IIC1.A
  N44: LCD1.K_-, LCM1602_IIC1.K
  N45: LCM1602_IIC1.LED_A, LCM1602_IIC1.LED_B
  N46: S1.Pin_1, S1.Pin_2, R10.Pin_1
  N47: S2.Pin_1, S2.Pin_2, R9.Pin_1
  N48: LED1.anode, R7.Pin_1
  N49: LED2.anode, R6.Pin_1
  N50: LED3.anode, R4.Pin_1
  N51: LED4.anode, R5.Pin_1
  N52: LED5.anode, R8.Pin_1

custom parts:
  Adafruit TCA9548A: You just found the perfect I2C sensor, and you want to wire up two or three or more of them to your Arduino when you realize "Uh oh, this chip has a fixed I2C address, and from what I know about I2C, you cannot have two devices with the same address on the same SDA/SCL pins!" Are you out of luck? You would be, if you didn't have this ultra-cool TCA9548A 1-to-8 I2C multiplexer! Finally, a way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
  20x4 LCD display: 20x4 character display. CHECK LED POLARITY BEFORE CONNECTING POWER Some versions of the dispaly have the polarity of the LED pins "A" and "K" reversed.
  LCM1602 IIC: I2C-Module to use a 1602 or 2004 LCD on with the wire.h libory Serial LCD Modul
  BME280: Temperature Humidity Barometric presure Sensor
  BH1750: Light Sensor
  gy-906: gy-906 Non-contact PIR I2C interface temperature sensor breakout board.
  ML8511 UV Sensor Breakout: Description: The ML8511 breakout is an easy to use ultraviolet light sensor. The MP8511 UV Sensor works by outputing an analog signal in relation to the amount of UV light it detects. This breakout can be very handy in creating devices that warn the user of sunburn or detect the UV index as it relates to weather conditions. This sensor breakout can detect 280-390nm light most effectively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
  MQ-135 Air Quality Sensor Module: The MQ-135 air quality sensor is one of range of MQ gas sensors that can be used to detect, measure, and monitor a wide range of gases, including NH3, NOx, CO2, benzene, and smoke, present in the atmosphere.
  KY-023 Dual Axis Joystick Module: KY-023 Dual-Axis Joystick Module.
  DFRobot Capacitive Soil Moisture Sensor V1.0: DFRobot Capacitive Soil Moisture Sensor V1.0 This product measures soil moisture levels by capacitive sensing, rather than resistive sensing like other types of moisture sensor. It is made of a corrosion resistant material giving it a long service life. Insert it into soil and impress your friends with the real-time soil moisture data! The product includes an on-board voltage regulator which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
  DS18B20 1-Wire Temperature Sensor Module: DS18B20 1-Wire Temperature Sensor Module The DS18B20 digital thermometer provides 9-bit to 12-bit Celsius temperature measurements and has an alarm function with nonvolatile user-programmable upper and lower trigger points. The DS18B20 communicates over a 1-Wire bus that by definition requires only one data line (and ground) for communication with a central microprocessor. In addition, the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
