# Fritzing sketch Diagrama Final - Arduino Uno (saved by Fritzing 1.0.4)
breadboards: 2

parts:
  LCD1 = 20x4 LCD display [part_number=2004A]
  LCM1602_IIC1 = LCM1602 IIC [part_number="LCM1602 IIC" chip_label="LCM1602 IIC" package="DIP (Dual Inline) [THT]"]
  ZS-042_RTC1 = ZS-042 RTC Module
  M1 = BME280
  Componente3 = BH1750
  Mod1 = gy-906
  M2 = MQ-135 Air Quality Sensor Module
  Capacitive_Soil_Moisture_Sensor1 = DFRobot Capacitive Soil Moisture Sensor V1.0 [part_number=SEN0193]
  microSD1 = MicroSD Card Module
  DS18B1 = DS18B20 1-Wire Temperature Sensor Module [part_number=DS18B20]
  R1 = Resistor [tolerance=±5% power=0.25W resistance=220 package=THT]
  S1 = Pushbutton [package="[THT]"]
  S2 = Pushbutton [package="[THT]"]
  LED1 = LED - 5mm [color="Red (633nm)" current=0.030A package="5 mm [THT]"]
  LED2 = LED - 5mm [color="Red (633nm)" current=0.030A package="5 mm [THT]"]
  LED3 = LED - 5mm [color="Red (633nm)" current=0.030A package="5 mm [THT]"]
  LED4 = LED - 5mm [color="Red (633nm)" current=0.030A package="5 mm [THT]"]
  LED5 = LED - 5mm [color="Red (633nm)" current=0.030A package="5 mm [THT]"]
  R3 = Resistor [tolerance=±5% power=0.25W resistance=220 package=THT]
  R4 = Resistor [tolerance=±5% power=0.25W resistance=220 package=THT]
  R5 = Resistor [tolerance=±5% power=0.25W resistance=220 package=THT]
  R6 = Resistor [tolerance=±5% power=0.25W resistance=220 package=THT]
  R7 = Resistor [tolerance=±5% power=0.25W resistance=220 package=THT]
  R8 = Resistor [tolerance=±5% power=0.25W resistance=220 package=THT]
  R9 = Resistor [tolerance=±5% power=0.25W resistance=220 package=THT]
  R10 = Resistor [tolerance=±5% power=0.25W resistance=220 package=THT]
  Componente5 = Arduino Uno (Rev3) - ICSP

nets:
  VSS: LCD1.Vss, LCM1602_IIC1.VSS
  VDD: LCD1.Vdd, LCM1602_IIC1.VDD
  N1: LCD1.Vo, LCM1602_IIC1.V0
  N2: LCD1.RS, LCM1602_IIC1.RS
  N3: LCD1.R/W, LCM1602_IIC1.RW
  N4: LCD1.E, LCM1602_IIC1.E
  N5: LCD1.DB0, LCM1602_IIC1.D0
  N6: LCD1.DB1, LCM1602_IIC1.D1
  N7: LCD1.DB2, LCM1602_IIC1.D2
  N8: LCD1.DB3, LCM1602_IIC1.D3
  N9: LCD1.DB4, LCM1602_IIC1.D4
  N10: LCD1.DB5, LCM1602_IIC1.D5
  N11: LCD1.DB6, LCM1602_IIC1.D6
  N12: LCD1.DB7, LCM1602_IIC1.D7
  N13: LCD1.A_+, LCM1602_IIC1.A
  N14: LCD1.K_-, LCM1602_IIC1.K
  GND: LCM1602_IIC1.GND, ZS-042_RTC1.GND, M1.GND, Componente3.GND, Mod1.GND, M2.GND, Capacitive_Soil_Moisture_Sensor1.GND, microSD1.GND, DS18B1.GND, R1.Pin_0, LED1.cathode, LED2.cathode, LED3.cathode, LED4.cathode, LED5.cathode, R3.Pin_1, R9.Pin_0, R10.Pin_0, Componente5.GND
  VCC: LCM1602_IIC1.VCC, ZS-042_RTC1.VCC, Componente3.VCC, Mod1.VIN, M2.VCC, Capacitive_Soil_Moisture_Sensor1.VCC, microSD1.VCC, DS18B1.VDD, Componente5.5V
  N15: LCM1602_IIC1.SDA, ZS-042_RTC1.SDA, M1.SDA, Componente3.SDA, Mod1.SDA, Componente5.A4/SDA
  N16: LCM1602_IIC1.SCL, ZS-042_RTC1.SCL, M1.SCL, Componente3.SCL, Mod1.SCL, Componente5.A5/SCL
  N17: LCM1602_IIC1.LED_A, LCM1602_IIC1.LED_B
  VIN: M1.VIN, Componente5.3V3
  N18: M2.AO, Componente5.A2
  N19: Capacitive_Soil_Moisture_Sensor1.A, Componente5.A3
  N20: microSD1.MISO, Componente5.ICSP_MISO, Componente5.D12/MISO
  N21: microSD1.MOSI, Componente5.D11_PWM/MOSI
  N22: microSD1.SCK, Componente5.D13/SCK
  N23: microSD1.CS, Componente5.D10_PWM/SS
  N24: DS18B1.OUT, R1.Pin_1, Componente5.D9_PWM
  N25: S1.Pin_1, S1.Pin_2, R10.Pin_1
  N26: S1.Pin_3, S1.Pin_4, Componente5.D8
  N27: S2.Pin_1, S2.Pin_2, R9.Pin_1
  N28: S2.Pin_3, S2.Pin_4, Componente5.D7
  N29: LED1.anode, R7.Pin_1
  N30: LED2.anode, R6.Pin_1
  N31: LED3.anode, R4.Pin_1
  N32: LED4.anode, R5.Pin_1
  N33: LED5.anode, R8.Pin_1
  N34: R4.Pin_0, Componente5.D6_PWM
  N35: R5.Pin_0, Componente5.D5_PWM
  N36: R6.Pin_0, Componente5.D4
  N37: R7.Pin_0, Componente5.D3_PWM
  N38: R8.Pin_0, Componente5.D2

custom parts:
  20x4 LCD display: 20x4 character display. CHECK LED POLARITY BEFORE CONNECTING POWER Some versions of the dispaly have the polarity of the LED pins "A" and "K" reversed.
  LCM1602 IIC: I2C-Module to use a 1602 or 2004 LCD on with the wire.h libory Serial LCD Modul
  BME280: Temperature Humidity Barometric presure Sensor
  BH1750: Light Sensor
  gy-906: gy-906 Non-contact PIR I2C interface temperature sensor breakout board.
  MQ-135 Air Quality Sensor Module: The MQ-135 air quality sensor is one of range of MQ gas sensors that can be used to detect, measure, and monitor a wide range of gases, including NH3, NOx, CO2, benzene, and smoke, present in the atmosphere.
  DFRobot Capacitive Soil Moisture Sensor V1.0: DFRobot Capacitive Soil Moisture Sensor V1.0 This product measures soil moisture levels by capacitive sensing, rather than resistive sensing like other types of moisture sensor. It is made of a corrosion resistant material giving it a long service life. Insert it into soil and impress your friends with the real-time soil moisture data! The product includes an on-board voltage regulator which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
  DS18B20 1-Wire Temperature Sensor Module: DS18B20 1-Wire Temperature Sensor Module The DS18B20 digital thermometer provides 9-bit to 12-bit Celsius temperature measurements and has an alarm function with nonvolatile user-programmable upper and lower trigger points. The DS18B20 communicates over a 1-Wire bus that by definition requires only one data line (and ground) for communication with a central microprocessor. In addition, the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
